# Fritzing sketch CrimeScout (saved by Fritzing 0.9.3b)

parts:
  ESP32_-_Back1 = ESP32 - CAM
  FC-1 = Sound Sensor

nets:
  N1: ESP32_-_Back1.GPIO0, FC-1.OUT
  GND: ESP32_-_Back1.GND, FC-1.GND
  N2: ESP32_-_Back1.3.3V_/_5V_/_P_OUT, FC-1.VCC

custom parts:
  ESP32 - CAM: The ESP32-CAM has a very competitive small-size camera module that can operate independently as a minimum system with a footprint of only 27*40.5*4.5mm and a deep sleep current of up to 6mA.
